# Fritzing sketch Coin_Changer (saved by Fritzing 0.9.3b)
breadboards: 2

parts:
  U1 = ESP32S-HiLetgo [part_number=ESP32S-HiLetgo]
  Part1 = Coin Acceptor - 6-Coin version
  A1 = Bill acceptor TB74-U
  HLK-PM1 = HLK-PM12 [part_number=HLK-PM12]
  M1 = RioRand LM2596
  J1 = Piezo Speaker
  RY1 = SSR-40VA
  A6 = yf-s401 flow sensor [package=THT]
  U2 = ESP32S-HiLetgo [part_number=ESP32S-HiLetgo]
  GY1 = MPU-6050 Board GY-521 [form="♀ (female)" package=THT]
  Part2 = LCD1602-I2C
  S1 = Momentary Switch [package=ksa_sealed_tac_switch]
  S2 = Momentary Switch [package=ksa_sealed_tac_switch]
  R1 = Resistor [tolerance=±5% resistance=220 package="0805 [SMD]"]
  R2 = Resistor [tolerance=±5% resistance=220 package="0805 [SMD]"]

nets:
  GND: U1.GND, Part1.GND, A1.Pin_1, A1.Pin_2, A1.Pin_3, HLK-PM1.-Vo, M1.Pin_2, M1.Pin_4, J1.pin1, RY1.Pin_4, U2.GND, GY1.pin2, Part2.GND, R1.Pin_1, R2.Pin_1
  VIN: U1.VIN, Part1.12V, M1.Pin_3, U2.VIN, Part2.VCC
  N1: U1.GPIO5, J1.pin2
  N2: U1.GPIO18, RY1.Pin_3
  N3: Part1.CTR, U2.GPIO27
  N4: Part1.SIG, U2.GPIO26
  N5: A1.Pin_4, U2.GPIO23
  N6: A1.Pin_5, U2.GPIO32
  N7: A1.Pin_6, HLK-PM1.+Vo, M1.Pin_1
  N8: HLK-PM1.AC_1, RY1.Pin_2
  N9: HLK-PM1.AC_2, A6.pin3
  N10: RY1.Pin_1, A6.pin1
  N11: U2.3.3, GY1.pin1
  N12: U2.GPIO18, S1.3, S1.4, R1.Pin_0
  N13: U2.GPIO19, S2.3, S2.4, R2.Pin_0
  N14: U2.GPIO21, GY1.pin4, Part2.SDA
  N15: U2.GPIO22, GY1.pin3, Part2.SCL
  N16: S1.1, S1.2
  N17: S2.1, S2.2

custom parts:
  ESP32S-HiLetgo: HiLetgo ESP-WROOM-32 ESP32 ESP-32S Development Board 2.4GHz Dual-Mode WiFi + Bluetooth Dual Cores Microcontroller The ESP32 integrated with Antenna switches, RF Balun, power amplifiers, low-noise amplifiers, filters, and management modules, and the entire solution occupies the least area of PCB. 2.4 GHz Wi-Fi plus Bluetooth dual-mode chip, with TSMC Ultra-low power consumption 40nm technology,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
  Coin Acceptor - 6-Coin version: 12V coin acceptor that can handle up to 6 different denominations. Output is either pulse width, serial, or single pin per coin value.
  Bill acceptor TB74-U: The TB-Series is the latest generation of banknote reader designed exclusively by TOPVME with the highest safety and acceptance rate have over 96%.
  SSR-40VA: SSR-40VA solid state relay.
  yf-s401 flow sensor: Flow sensors sit in line with your water line, and uses a pinwheel sensor to measure how much liquid has moved through it.
  MPU-6050 Board GY-521: Acelerometro y Giroscopio MPU-6050 Board GY-521
  LCD1602-I2C: A standard character display, usually with 2x16 characters. Comes in many colors with LCM1602 IIC attached.
